// Logisim project y86.circ as structural Verilog: 24 circuits, main circuit ALU
module ALU (
  input  [7:0] A,
  input  [7:0] B,
  input  Cin,
  input  [3:0] OP,
  output ZF,
  output SF,
  output [7:0] F,
  output OF,
  output Cout
);

  wire addl_1_cout, addl_1_of, andl_1_of, asrl_1_cout, asrl_1_of, iszero_1_out_2, lsll_1_cout, lsll_1_of,
       subl_1_cout, subl_1_of, xorl_1_of;
  wire [7:0] addl_1_f, andl_1_f, asrl_1_f, lsll_1_f, subl_1_f, xorl_1_f;

  addl addl_1 (.Cin(Cin), .A(A), .F(addl_1_f), .B(B), .Cout(addl_1_cout), .OF(addl_1_of));
  subl subl_1 (.Cin(Cin), .A(A), .F(subl_1_f), .B(B), .Cout(subl_1_cout), .OF(subl_1_of));
  andl andl_1 (.A(A), .B(B), .F(andl_1_f), .OF(andl_1_of));
  xorl xorl_1 (.A(A), .B(B), .F(xorl_1_f), .OF(xorl_1_of));
  asrl asrl_1 (.A(A), .F(asrl_1_f), .Cout(asrl_1_cout), .OF(asrl_1_of));
  lsll lsll_1 (.A(A), .F(lsll_1_f), .OF(lsll_1_of), .Cout(lsll_1_cout));
  Multiplexer #(.select(4), .enable("false")) multiplexer_1 (
    .in0(addl_1_of), .in1(subl_1_of), .in2(andl_1_of), .in3(xorl_1_of), .in4(asrl_1_of), .in5(lsll_1_of),
    .out(OF), .sel(OP));  // open: in6, in7, in8, in9, in10, in11, in12, in13, in14, in15
  Multiplexer #(.select(4), .enable("false")) multiplexer_2 (
    .in0(addl_1_cout), .in1(subl_1_cout), .in4(asrl_1_cout), .in5(lsll_1_cout), .out(Cout), .sel(OP));  // open: in2, in3, in6, in7, in8, in9, in10, in11, in12, in13, in14, in15
  Multiplexer #(.select(4), .width(8), .enable("false")) multiplexer_3 (
    .in0(addl_1_f), .in1(subl_1_f), .in2(andl_1_f), .in3(xorl_1_f), .in4(asrl_1_f), .in5(lsll_1_f), .out(F),
    .sel(OP));  // open: in6, in7, in8, in9, in10, in11, in12, in13, in14, in15
  not not_1 (ZF, iszero_1_out_2);
  isZero iszero_1 (.in_1(F), .out_2(iszero_1_out_2));

  assign SF = F[7];
endmodule

module addl (
  input  Cin,
  input  [7:0] A,
  input  [7:0] B,
  output [7:0] F,
  output Cout,
  output OF
);

  wire and_1_out, and_2_out, fullbitadder_1_cout, fullbitadder_2_cout, fullbitadder_3_cout,
       fullbitadder_4_cout, fullbitadder_5_cout, fullbitadder_6_cout, fullbitadder_8_cout, not_1_out,
       not_2_out, not_3_out;

  fullBitAdder fullbitadder_1 (.A(A[1]), .B(B[1]), .Cin(fullbitadder_2_cout), .sum(F[1]), .Cout(fullbitadder_1_cout));
  fullBitAdder fullbitadder_2 (.A(A[0]), .B(B[0]), .Cin(Cin), .sum(F[0]), .Cout(fullbitadder_2_cout));
  fullBitAdder fullbitadder_3 (.A(A[2]), .B(B[2]), .Cin(fullbitadder_1_cout), .sum(F[2]), .Cout(fullbitadder_3_cout));
  fullBitAdder fullbitadder_4 (.A(A[4]), .B(B[4]), .Cin(fullbitadder_5_cout), .sum(F[4]), .Cout(fullbitadder_4_cout));
  fullBitAdder fullbitadder_5 (.A(A[3]), .B(B[3]), .Cin(fullbitadder_3_cout), .sum(F[3]), .Cout(fullbitadder_5_cout));
  fullBitAdder fullbitadder_6 (.A(A[5]), .B(B[5]), .Cin(fullbitadder_4_cout), .sum(F[5]), .Cout(fullbitadder_6_cout));
  fullBitAdder fullbitadder_7 (.A(A[7]), .B(B[7]), .Cin(fullbitadder_8_cout), .sum(F[7]), .Cout(Cout));
  fullBitAdder fullbitadder_8 (.A(A[6]), .B(B[6]), .Cin(fullbitadder_6_cout), .sum(F[6]), .Cout(fullbitadder_8_cout));
  not not_1 (not_1_out, B[7]);
  not not_2 (not_2_out, A[7]);
  and and_1 (and_1_out, A[7], not_3_out, B[7]);
  not not_3 (not_3_out, F[7]);
  and and_2 (and_2_out, not_1_out, F[7], not_2_out);
  or or_1 (OF, and_1_out, and_2_out);
endmodule

module subl (
  input  Cin,
  input  [7:0] A,
  input  [7:0] B,
  output [7:0] F,
  output Cout,
  output OF
);

  wire and_1_out, and_2_out, fullbitsubtracter_1_cout, fullbitsubtracter_2_cout, fullbitsubtracter_3_cout,
       fullbitsubtracter_4_cout, fullbitsubtracter_5_cout, fullbitsubtracter_6_cout,
       fullbitsubtracter_7_cout, not_1_out, not_2_out, not_3_out;

  fullBitSubtracter fullbitsubtracter_1 (
    .A(A[1]), .B(B[1]), .Cin(fullbitsubtracter_2_cout), .sum(F[1]), .Cout(fullbitsubtracter_1_cout));
  fullBitSubtracter fullbitsubtracter_2 (.A(A[0]), .B(B[0]), .Cin(Cin), .sum(F[0]), .Cout(fullbitsubtracter_2_cout));
  fullBitSubtracter fullbitsubtracter_3 (
    .A(A[2]), .B(B[2]), .Cin(fullbitsubtracter_1_cout), .sum(F[2]), .Cout(fullbitsubtracter_3_cout));
  fullBitSubtracter fullbitsubtracter_4 (
    .A(A[4]), .B(B[4]), .Cin(fullbitsubtracter_5_cout), .sum(F[4]), .Cout(fullbitsubtracter_4_cout));
  fullBitSubtracter fullbitsubtracter_5 (
    .A(A[3]), .B(B[3]), .Cin(fullbitsubtracter_3_cout), .sum(F[3]), .Cout(fullbitsubtracter_5_cout));
  fullBitSubtracter fullbitsubtracter_6 (
    .A(A[5]), .B(B[5]), .Cin(fullbitsubtracter_4_cout), .sum(F[5]), .Cout(fullbitsubtracter_6_cout));
  fullBitSubtracter fullbitsubtracter_7 (
    .A(A[6]), .B(B[6]), .Cin(fullbitsubtracter_6_cout), .sum(F[6]), .Cout(fullbitsubtracter_7_cout));
  fullBitSubtracter fullbitsubtracter_8 (.A(A[7]), .B(B[7]), .Cin(fullbitsubtracter_7_cout), .sum(F[7]), .Cout(Cout));
  not not_1 (not_1_out, F[7]);
  and and_1 (and_1_out, A[7], not_1_out, not_2_out);
  not not_2 (not_2_out, B[7]);
  not not_3 (not_3_out, A[7]);
  and and_2 (and_2_out, not_3_out, F[7], B[7]);
  or or_1 (OF, and_1_out, and_2_out);
endmodule

module andl (
  input  [7:0] A,
  input  [7:0] B,
  output OF,
  output [7:0] F
);

  assign F = A & B;  // AND_Gate and_1, 8 bits wide

  assign OF = 1'b0;
endmodule

module xorl (
  input  [7:0] A,
  input  [7:0] B,
  output OF,
  output [7:0] F
);

  assign F = A | B;  // OR_Gate or_1, 8 bits wide

  assign OF = 1'b0;
endmodule

module asrl (
  input  [7:0] A,
  output OF,
  output Cout,
  output [7:0] F
);


  assign Cout = A[0];
  assign F = {{2{A[7]}}, A[6:1]};
  assign OF = 1'b0;
endmodule

module lsll (
  input  [7:0] A,
  output OF,
  output [7:0] F,
  output Cout
);


  assign Cout = A[7];
  assign F = {A[6:0], 1'b0};
  assign OF = 1'b0;
endmodule

module fullBitAdder (
  input  A,
  input  B,
  input  Cin,
  output sum,
  output Cout
);

  wire and_1_out, and_2_out, xor_1_out, xor_2_out;

  xor xor_1 (xor_1_out, A, B);
  and and_1 (and_1_out, A, B);
  and and_2 (and_2_out, Cin, xor_2_out);
  xor xor_2 (xor_2_out, A, B);
  xor xor_3 (sum, xor_1_out, Cin);
  or or_1 (Cout, and_1_out, and_2_out);
endmodule

module fullBitSubtracter (
  input  A,
  input  B,
  input  Cin,
  output sum,
  output Cout
);

  wire and_1_out, and_2_out, and_3_out, not_1_out, not_2_out, or_1_out, xor_1_out;

  not not_1 (not_1_out, A);
  not not_2 (not_2_out, A);
  xor xor_1 (xor_1_out, A, B);
  and and_1 (and_1_out, not_1_out, Cin);
  and and_2 (and_2_out, not_2_out, B);
  xor xor_2 (sum, xor_1_out, Cin);
  or or_1 (or_1_out, and_1_out, and_2_out);
  and and_3 (and_3_out, B, Cin);
  or or_2 (Cout, or_1_out, and_3_out);
endmodule

module isZero (
  input  [7:0] in_1,
  output out_2
);

  or or_1 (out_2, in_1[0], in_1[1], in_1[2], in_1[3], in_1[4], in_1[5], in_1[6], in_1[7]);
endmodule

module Align (
  input  [7:0] B1,
  input  [7:0] B2,
  input  [7:0] B3,
  input  [7:0] B4,
  input  [7:0] B5,
  input  [7:0] B6,
  input  [7:0] B7,
  input  [7:0] B8,
  input  [7:0] B9,
  input  NeedRegs,
  output [3:0] rA,
  output [3:0] rB,
  output [31:0] valC_1,
  output [31:0] valC_0
);
endmodule

module dmem (
  input  [31:0] Addr_1,
  input  [31:0] Addr_0,
  input  [31:0] Data_1,
  input  [31:0] Data_0,
  input  read,
  input  write,
  input  clock,
  input  dataclear,
  output [31:0] valM_1,
  output [31:0] valM_0,
  output dmemerr
);

  wire bitfinder_1_found, bitfinder_2_found, or_1_out, or_2_out;
  wire [6:0] adder_1_out, multiplexer_1_out, multiplexer_2_out;
  wire [31:0] ram_1_data, ram_2_data;

  BitFinder #(.width(32)) bitfinder_1 (.in(Addr_1), .found(bitfinder_1_found));  // open: index
  BitFinder #(.width(22)) bitfinder_2 (.in(Addr_0[31:10]), .found(bitfinder_2_found));  // open: index
  or or_1 (or_1_out, bitfinder_1_found, bitfinder_2_found, Addr_0[1], Addr_0[0]);
  Adder #(.width(7)) adder_1 (.a({7{1'b0}}), .b(Addr_0[9:3]), .out(adder_1_out));  // open: cin, cout
  or or_2 (or_2_out, read, write, or_1_out);
  and and_1 (dmemerr, or_1_out, or_2_out);
  Multiplexer #(.width(7), .enable("false")) multiplexer_1 (
    .in0({7{1'b0}}), .in1(adder_1_out), .out(multiplexer_1_out), .sel(or_2_out));
  Multiplexer #(.width(7), .enable("false")) multiplexer_2 (
    .in0({7{1'b0}}), .in1(Addr_0[9:3]), .out(multiplexer_2_out), .sel(or_2_out));
  RAM #(.addrWidth(7), .dataWidth(32)) ram_1 (
    .addr(multiplexer_1_out), .data(ram_1_data), .clk(clock), .ld(or_2_out), .clr(dataclear));  // open: sel
  RAM #(.addrWidth(7), .dataWidth(32)) ram_2 (
    .addr(multiplexer_2_out), .data(ram_2_data), .clk(clock), .ld(or_2_out), .clr(dataclear));  // open: sel
  Multiplexer #(.width(32), .enable("false")) multiplexer_3 (
    .in0(ram_1_data), .in1(ram_2_data), .out(valM_0), .sel(Addr_0[2]));
  Multiplexer #(.width(32), .enable("false")) multiplexer_4 (
    .in0(ram_2_data), .in1(ram_1_data), .out(valM_1), .sel(Addr_0[2]));
endmodule

module imem (
  input  [31:0] in_1,
  output [7:0] out_2,
  output [7:0] out_3,
  output [7:0] out_4,
  output [7:0] out_5,
  output [7:0] out_6,
  output [7:0] out_7,
  output [7:0] out_8,
  output [7:0] out_9,
  output [7:0] out_10,
  output imemerr,
  output [7:0] out_12
);

  wire bankaddr_1_error, bankaddr_2_error, bankaddr_3_error, bankaddr_4_error;
  wire [3:0] low4_1_out_2;
  wire [7:0] bankaddr_1_bankaddr, bankaddr_2_bankaddr, bankaddr_3_bankaddr, bankaddr_4_bankaddr;
  wire [31:0] rom_1_data, rom_2_data, rom_3_data, rom_4_data;

  Low4 low4_1 (.in_1(in_1), .out_2(low4_1_out_2));
  BankAddr bankaddr_1 (.BankIndex(2'b00), .FullAddr(in_1), .BankAddr(bankaddr_1_bankaddr), .Error(bankaddr_1_error));
  BankAddr bankaddr_2 (.BankIndex(2'b01), .FullAddr(in_1), .BankAddr(bankaddr_2_bankaddr), .Error(bankaddr_2_error));
  BankAddr bankaddr_3 (.BankIndex(2'b10), .FullAddr(in_1), .BankAddr(bankaddr_3_bankaddr), .Error(bankaddr_3_error));
  BankAddr bankaddr_4 (.BankIndex(2'b11), .FullAddr(in_1), .BankAddr(bankaddr_4_bankaddr), .Error(bankaddr_4_error));
  or or_1 (imemerr, bankaddr_1_error, bankaddr_2_error, bankaddr_3_error, bankaddr_4_error);
  ROM #(.dataWidth(32)) rom_1 (.addr(bankaddr_1_bankaddr), .data(rom_1_data));  // open: sel
  ROM #(.dataWidth(32)) rom_2 (.addr(bankaddr_2_bankaddr), .data(rom_2_data));  // open: sel
  ROM #(.dataWidth(32)) rom_3 (.addr(bankaddr_3_bankaddr), .data(rom_3_data));  // open: sel
  ROM #(.dataWidth(32)) rom_4 (.addr(bankaddr_4_bankaddr), .data(rom_4_data));  // open: sel
  BankMux4 bankmux4_1 (
    .Bank0(rom_1_data), .Bank1(rom_2_data), .Bank2(rom_3_data), .Bank3(rom_4_data), .AddrLow(low4_1_out_2),
    .Index(4'b0000), .OutByte(out_2));
  BankMux4 bankmux4_2 (
    .Bank0(rom_1_data), .Bank1(rom_2_data), .Bank2(rom_3_data), .Bank3(rom_4_data), .AddrLow(low4_1_out_2),
    .Index(4'b0001), .OutByte(out_3));
  BankMux4 bankmux4_3 (
    .Bank0(rom_1_data), .Bank1(rom_2_data), .Bank2(rom_3_data), .Bank3(rom_4_data), .AddrLow(low4_1_out_2),
    .Index(4'b0010), .OutByte(out_4));
  BankMux4 bankmux4_4 (
    .Bank0(rom_1_data), .Bank1(rom_2_data), .Bank2(rom_3_data), .Bank3(rom_4_data), .AddrLow(low4_1_out_2),
    .Index(4'b0011), .OutByte(out_5));
  BankMux4 bankmux4_5 (
    .Bank0(rom_1_data), .Bank1(rom_2_data), .Bank2(rom_3_data), .Bank3(rom_4_data), .AddrLow(low4_1_out_2),
    .Index(4'b0100), .OutByte(out_6));
  BankMux4 bankmux4_6 (
    .Bank0(rom_1_data), .Bank1(rom_2_data), .Bank2(rom_3_data), .Bank3(rom_4_data), .AddrLow(low4_1_out_2),
    .Index(4'b0101), .OutByte(out_7));
  BankMux4 bankmux4_7 (
    .Bank0(rom_1_data), .Bank1(rom_2_data), .Bank2(rom_3_data), .Bank3(rom_4_data), .AddrLow(low4_1_out_2),
    .Index(4'b0110), .OutByte(out_8));
  BankMux4 bankmux4_8 (
    .Bank0(rom_1_data), .Bank1(rom_2_data), .Bank2(rom_3_data), .Bank3(rom_4_data), .AddrLow(low4_1_out_2),
    .Index(4'b0111), .OutByte(out_9));
  BankMux4 bankmux4_9 (
    .Bank0(rom_1_data), .Bank1(rom_2_data), .Bank2(rom_3_data), .Bank3(rom_4_data), .AddrLow(low4_1_out_2),
    .Index(4'b1000), .OutByte(out_10));
  BankMux4 bankmux4_10 (
    .Bank0(rom_1_data), .Bank1(rom_2_data), .Bank2(rom_3_data), .Bank3(rom_4_data), .AddrLow(low4_1_out_2),
    .Index(4'b1001), .OutByte(out_12));

  // Notes on the sheet:
  //   contents of rom_1 (hex, n*v repeats v):
  //   30f00500 0 0 4000000
  //   contents of rom_2 (hex, n*v repeats v):
  //   0 60306001 40060000
  //   contents of rom_3 (hex, n*v repeats v):
  //   30f3 603130f6
  //   contents of rom_4 (hex, n*v repeats v):
  //   3000000 3c000000 4016
endmodule

module Low4 (
  input  [31:0] in_1,
  output [3:0] out_2
);


  assign out_2 = in_1[3:0];
endmodule

module BankAddr (
  input  [1:0] BankIndex,
  input  [31:0] FullAddr,
  output [7:0] BankAddr,
  output Error
);

  wire subtractor_1_bout;

  // Probe on FullAddr
  // Probe on FullAddr[3:2]
  Subtractor #(.width(2)) subtractor_1 (.a(BankIndex), .b(FullAddr[3:2]), .bout(subtractor_1_bout));  // open: out, bin
  Adder adder_1 (.a({8{1'b0}}), .b(FullAddr[11:4]), .out(BankAddr), .cin(subtractor_1_bout));  // open: cout
  or or_1 (Error, FullAddr[12], FullAddr[13], FullAddr[14], FullAddr[15], FullAddr[16], FullAddr[17], FullAddr[18], FullAddr[19], FullAddr[20], FullAddr[21], FullAddr[22], FullAddr[23], FullAddr[24], FullAddr[25], FullAddr[26], FullAddr[27], FullAddr[28], FullAddr[29], FullAddr[30], FullAddr[31]);
endmodule

module BankMux4 (
  input  [31:0] Bank0,
  input  [31:0] Bank1,
  input  [31:0] Bank2,
  input  [31:0] Bank3,
  input  [3:0] AddrLow,
  input  [3:0] Index,
  output [7:0] OutByte
);

  wire [3:0] adder_1_out;

  Adder #(.width(4)) adder_1 (.a(AddrLow), .b(Index), .out(adder_1_out));  // open: cin, cout
  Multiplexer #(.select(4), .width(8), .enable("false")) multiplexer_1 (
    .in0(Bank0[31:24]), .in1(Bank0[23:16]), .in2(Bank0[15:8]), .in3(Bank0[7:0]), .in4(Bank1[31:24]),
    .in5(Bank1[23:16]), .in6(Bank1[15:8]), .in7(Bank1[7:0]), .in8(Bank2[31:24]), .in9(Bank2[23:16]),
    .in10(Bank2[15:8]), .in11(Bank2[7:0]), .in12(Bank3[31:24]), .in13(Bank3[23:16]), .in14(Bank3[15:8]),
    .in15(Bank3[7:0]), .out(OutByte), .sel(adder_1_out));
endmodule

module regfile (
  input  [3:0] srcA,
  input  [3:0] srcB,
  input  [3:0] dstE,
  input  [31:0] valE_1,
  input  [31:0] valE_0,
  input  [3:0] dstM,
  input  [31:0] valM_1,
  input  [31:0] valM_0,
  input  in_9,
  input  in_10,
  output [31:0] valA_1,
  output [31:0] valA_0,
  output [31:0] valB_1,
  output [31:0] valB_0
);

  wire and_1_out, and_2_out, and_3_out, and_4_out, msb4_1_msb, msb4_2_msb, msb4_3_msb, msb4_4_msb,
       regwriteenable_1_enable, regwriteenable_2_enable;
  wire [2:0] msb4_1_lower3, msb4_2_lower3, msb4_3_lower3, msb4_4_lower3;
  wire [31:0] regs8x32_1_vala, regs8x32_1_valb, regs8x32_2_vala, regs8x32_2_valb, regs8x32_3_vala,
       regs8x32_3_valb, regs8x32_4_vala, regs8x32_4_valb;

  msb4 msb4_1 (.in_1(srcA), .msb(msb4_1_msb), .lower3(msb4_1_lower3));
  msb4 msb4_2 (.in_1(srcB), .msb(msb4_2_msb), .lower3(msb4_2_lower3));
  regwriteenable regwriteenable_1 (.\reg (dstE), .enable(regwriteenable_1_enable));
  msb4 msb4_3 (.in_1(dstE), .msb(msb4_3_msb), .lower3(msb4_3_lower3));
  regwriteenable regwriteenable_2 (.\reg (dstM), .enable(regwriteenable_2_enable));
  msb4 msb4_4 (.in_1(dstM), .msb(msb4_4_msb), .lower3(msb4_4_lower3));
  buf and_1 (and_1_out, ~regwriteenable_1_enable);  // AND_Gate AND_Gate
  and and_2 (and_2_out, msb4_3_lower3[0], regwriteenable_1_enable, msb4_3_msb);
  buf and_3 (and_3_out, ~regwriteenable_2_enable);  // AND_Gate AND_Gate
  and and_4 (and_4_out, regwriteenable_2_enable, msb4_4_msb);
  Regs8x32 regs8x32_1 (
    .srcA(msb4_1_lower3), .srcB(msb4_2_lower3), .dstEenable(and_1_out), .dstE(msb4_3_lower3), .valE(valE_1),
    .dstMenable(and_3_out), .dstM(msb4_4_lower3), .valM(valM_1), .Clock(in_9), .Clear(in_10),
    .valA(regs8x32_1_vala), .valB(regs8x32_1_valb));
  Regs8x32 regs8x32_2 (
    .srcA(msb4_1_lower3), .srcB(msb4_2_lower3), .dstEenable(and_1_out), .dstE(msb4_3_lower3), .valE(valE_0),
    .dstMenable(and_3_out), .dstM(msb4_4_lower3), .valM(valM_0), .Clock(in_9), .Clear(in_10),
    .valA(regs8x32_2_vala), .valB(regs8x32_2_valb));
  Regs8x32 regs8x32_3 (
    .srcA(msb4_1_lower3), .srcB(msb4_2_lower3), .dstEenable(and_2_out), .dstE(msb4_3_lower3), .valE(valE_1),
    .dstMenable(and_4_out), .dstM(msb4_4_lower3), .valM(valM_1), .Clock(in_9), .Clear(in_10),
    .valA(regs8x32_3_vala), .valB(regs8x32_3_valb));
  Regs8x32 regs8x32_4 (
    .srcA(msb4_1_lower3), .srcB(msb4_2_lower3), .dstEenable(and_2_out), .dstE(msb4_3_lower3), .valE(valE_0),
    .dstMenable(and_4_out), .dstM(msb4_4_lower3), .valM(valM_0), .Clock(in_9), .Clear(in_10),
    .valA(regs8x32_4_vala), .valB(regs8x32_4_valb));
  Multiplexer #(.width(32), .enable("false")) multiplexer_1 (
    .in0(regs8x32_1_vala), .in1(regs8x32_3_vala), .out(valA_1), .sel(msb4_1_msb));
  Multiplexer #(.width(32), .enable("false")) multiplexer_2 (
    .in0(regs8x32_2_vala), .in1(regs8x32_4_vala), .out(valA_0), .sel(msb4_1_msb));
  Multiplexer #(.width(32), .enable("false")) multiplexer_3 (
    .in0(regs8x32_1_valb), .in1(regs8x32_3_valb), .out(valB_1), .sel(msb4_2_msb));
  Multiplexer #(.width(32), .enable("false")) multiplexer_4 (
    .in0(regs8x32_2_valb), .in1(regs8x32_4_valb), .out(valB_0), .sel(msb4_2_msb));
  // Pins of 1 and 3 bits meet at msb4_3_lower3

  // Notes on the sheet:
  //   Regs0-7MS
  //   Regs0-7LS
  //   Regs8-15MS
  //   Regs8-15LS
endmodule

module Regs8x32 (
  input  [2:0] srcA,
  input  [2:0] srcB,
  input  dstEenable,
  input  [2:0] dstE,
  input  [31:0] valE,
  input  dstMenable,
  input  [2:0] dstM,
  input  [31:0] valM,
  input  Clock,
  input  Clear,
  output [31:0] valA,
  output [31:0] valB
);

  wire demultiplexer_1_out0, demultiplexer_1_out1, demultiplexer_1_out2, demultiplexer_1_out3,
       demultiplexer_1_out4, demultiplexer_1_out5, demultiplexer_1_out6, demultiplexer_1_out7,
       demultiplexer_2_out0, demultiplexer_2_out1, demultiplexer_2_out2, demultiplexer_2_out3,
       demultiplexer_2_out4, demultiplexer_2_out5, demultiplexer_2_out6, demultiplexer_2_out7,
       regwrite_1_enable, regwrite_2_enable, regwrite_3_enable, regwrite_4_enable, regwrite_5_enable,
       regwrite_6_enable, regwrite_7_enable, regwrite_8_enable;
  wire [31:0] register_1_q, register_2_q, register_4_q, register_5_q, register_6_q, register_7_q,
       register_8_q, regwrite_1_data, regwrite_2_data, regwrite_3_data, regwrite_4_data, regwrite_5_data,
       regwrite_6_data, regwrite_7_data, regwrite_8_data;

  Demultiplexer #(.select(3), .enable("false")) demultiplexer_1 (
    .out0(demultiplexer_1_out0), .out1(demultiplexer_1_out1), .out2(demultiplexer_1_out2),
    .out3(demultiplexer_1_out3), .out4(demultiplexer_1_out4), .out5(demultiplexer_1_out5),
    .out6(demultiplexer_1_out6), .out7(demultiplexer_1_out7), .in(dstEenable), .sel(dstE));
  Demultiplexer #(.select(3), .enable("false")) demultiplexer_2 (
    .out0(demultiplexer_2_out0), .out1(demultiplexer_2_out1), .out2(demultiplexer_2_out2),
    .out3(demultiplexer_2_out3), .out4(demultiplexer_2_out4), .out5(demultiplexer_2_out5),
    .out6(demultiplexer_2_out6), .out7(demultiplexer_2_out7), .in(dstMenable), .sel(dstM));
  RegWrite regwrite_1 (
    .dstE(demultiplexer_1_out0), .dstM(demultiplexer_2_out0), .valE(valE), .valM(valM),
    .Data(regwrite_1_data), .Enable(regwrite_1_enable));
  RegWrite regwrite_2 (
    .dstE(demultiplexer_1_out1), .dstM(demultiplexer_2_out1), .valE(valE), .valM(valM),
    .Data(regwrite_2_data), .Enable(regwrite_2_enable));
  RegWrite regwrite_3 (
    .dstE(demultiplexer_1_out2), .dstM(demultiplexer_2_out2), .valE(valE), .valM(valM),
    .Data(regwrite_3_data), .Enable(regwrite_3_enable));
  RegWrite regwrite_4 (
    .dstE(demultiplexer_1_out3), .dstM(demultiplexer_2_out3), .valE(valE), .valM(valM),
    .Data(regwrite_4_data), .Enable(regwrite_4_enable));
  RegWrite regwrite_5 (
    .dstE(demultiplexer_1_out4), .dstM(demultiplexer_2_out4), .valE(valE), .valM(valM),
    .Data(regwrite_5_data), .Enable(regwrite_5_enable));
  RegWrite regwrite_6 (
    .dstE(demultiplexer_1_out5), .dstM(demultiplexer_2_out5), .valE(valE), .valM(valM),
    .Data(regwrite_6_data), .Enable(regwrite_6_enable));
  RegWrite regwrite_7 (
    .dstE(demultiplexer_1_out6), .dstM(demultiplexer_2_out6), .valE(valE), .valM(valM),
    .Data(regwrite_7_data), .Enable(regwrite_7_enable));
  RegWrite regwrite_8 (
    .dstE(demultiplexer_1_out7), .dstM(demultiplexer_2_out7), .valE(valE), .valM(valM),
    .Data(regwrite_8_data), .Enable(regwrite_8_enable));
  Register #(.width(32)) register_1 (
    .D(regwrite_1_data), .en(regwrite_1_enable), .Q(register_1_q), .clk(Clock), .clr(Clear));
  Register #(.width(32)) register_2 (
    .D(regwrite_2_data), .en(regwrite_2_enable), .Q(register_2_q), .clk(Clock), .clr(Clear));
  Register #(.width(32)) register_3 (
    .D(regwrite_3_data), .en(regwrite_3_enable), .Q(register_2_q), .clk(Clock), .clr(Clear));
  Register #(.width(32)) register_4 (
    .D(regwrite_4_data), .en(regwrite_4_enable), .Q(register_4_q), .clk(Clock), .clr(Clear));
  Register #(.width(32)) register_5 (
    .D(regwrite_5_data), .en(regwrite_5_enable), .Q(register_5_q), .clk(Clock), .clr(Clear));
  Register #(.width(32)) register_6 (
    .D(regwrite_6_data), .en(regwrite_6_enable), .Q(register_6_q), .clk(Clock), .clr(Clear));
  Register #(.width(32)) register_7 (
    .D(regwrite_7_data), .en(regwrite_7_enable), .Q(register_7_q), .clk(Clock), .clr(Clear));
  Register #(.width(32)) register_8 (
    .D(regwrite_8_data), .en(regwrite_8_enable), .Q(register_8_q), .clk(Clock), .clr(Clear));
  Multiplexer #(.select(3), .width(32), .enable("false")) multiplexer_1 (
    .in0(register_1_q), .in1(register_2_q), .in2(register_2_q), .in3(register_4_q), .in4(register_5_q),
    .in5(register_6_q), .in6(register_7_q), .in7(register_8_q), .out(valA), .sel(srcA));
  Multiplexer #(.select(3), .width(32), .enable("false")) multiplexer_2 (
    .in0(register_1_q), .in1(register_2_q), .in2(register_2_q), .in3(register_4_q), .in4(register_5_q),
    .in5(register_6_q), .in6(register_7_q), .in7(register_8_q), .out(valB), .sel(srcB));
endmodule

module RegWrite (
  input  dstE,
  input  dstM,
  input  [31:0] valE,
  input  [31:0] valM,
  output [31:0] Data,
  output Enable
);

  or or_1 (Enable, dstE, dstM);
  Multiplexer #(.width(32), .enable("false")) multiplexer_1 (.in0(valE), .in1(valM), .out(Data), .sel(dstM));
endmodule

module msb4 (
  input  [3:0] in_1,
  output msb,
  output [2:0] lower3
);


  assign lower3 = in_1[2:0];
  assign msb = in_1[3];
endmodule

module regwriteenable (
  input  [3:0] \reg ,
  output enable
);

  wire and_1_out;

  and and_1 (and_1_out, \reg [3], \reg [2], \reg [1], \reg [0]);
  not not_1 (enable, and_1_out);
endmodule

module main (
  input  Reset
);

  wire and_1_out, clock_1_out, nor_1_out, not_1_out;
  wire [1:0] Stat_q, undriven;
  wire [31:0] PC_q, PChold_q;

  and and_1 (and_1_out, clock_1_out, nor_1_out);
  Clock clock_1 (.out(clock_1_out));
  Register #(.width(32)) PC (.D(PChold_q), .Q(PC_q), .clk(and_1_out), .clr(Reset));  // open: en
  nor nor_1 (nor_1_out, Stat_q[1], Stat_q[0]);
  not not_1 (not_1_out, and_1_out);
  Register #(.width(2)) Stat (.D(undriven), .Q(Stat_q), .clk(not_1_out));  // open: en, clr
  Register #(.width(32)) PChold (.Q(PChold_q), .clk(not_1_out), .clr(Reset));  // open: D, en
endmodule

module ALU32 (
  input  [31:0] A,
  input  [31:0] B,
  input  Cin,
  input  [3:0] Oper,
  output ZF,
  output [31:0] F,
  output OF_32_1,
  output Cout,
  output SF
);

  wire alu_1_cout, alu_1_zf, alu_2_cout, alu_2_zf, alu_3_cout, alu_3_zf, alu_4_zf;

  ALU alu_1 (
    .A(A[7:0]), .B(B[7:0]), .Cin(Cin), .Cout(alu_1_cout), .ZF(alu_1_zf), .OP(Oper), .F(F[7:0]));  // open: OF, SF
  ALU alu_2 (
    .A(A[15:8]), .B(B[15:8]), .Cin(alu_1_cout), .Cout(alu_2_cout), .ZF(alu_2_zf), .OP(Oper), .F(F[15:8]));  // open: OF, SF
  ALU alu_3 (
    .A(A[23:16]), .B(B[23:16]), .Cin(alu_2_cout), .Cout(alu_3_cout), .ZF(alu_3_zf), .OP(Oper), .F(F[23:16]));  // open: OF, SF
  ALU alu_4 (
    .A(A[31:24]), .B(B[31:24]), .Cin(alu_3_cout), .OF(OF_32_1), .Cout(Cout), .ZF(alu_4_zf), .OP(Oper),
    .SF(SF), .F(F[31:24]));
  and and_1 (ZF, alu_1_zf, alu_2_zf, alu_3_zf, alu_4_zf);

  // Other names for the same wires on the sheet: A1[7:0] = A[7:0]; A2[7:0] = A[15:8]; A3[7:0] = A[23:16];
  //   A4[7:0] = A[31:24]; B1[7:0] = B[7:0]; B2[7:0] = B[15:8]; B3[7:0] = B[23:16]; B4[7:0] = B[31:24];
  //   F1[7:0] = F[7:0]; F2[7:0] = F[15:8]; F3[7:0] = F[23:16]; F4[7:0] = F[31:24]
endmodule

module ALU64 (
  input  [31:0] AM,
  input  [31:0] Al,
  input  [31:0] Bl,
  input  [31:0] BM,
  input  [3:0] OPER,
  output ZF,
  output OF,
  output Cout,
  output SF,
  output [31:0] Fl,
  output [31:0] Fm
);

  wire ALU32_1_cout;

  ALU32 ALU32_1 (.Cin(1'b0), .Oper(OPER), .A(Al), .B(Bl), .F(Fl), .Cout(ALU32_1_cout));  // open: ZF, OF_32_1, SF
  ALU32 ALU32_2 (.Cin(ALU32_1_cout), .Oper(OPER), .A(AM), .B(BM), .ZF(ZF), .F(Fm), .OF_32_1(OF), .Cout(Cout), .SF(SF));

  // Other names for the same wires on the sheet: F_l[31:0] = Fl; F_m[31:0] = Fm
endmodule
